# Fritzing sketch alarma pir-ultras-guille (saved by Fritzing 0.9.3b)

parts:
  Componente1 = Arduino Nano (Rev3.0)
  R1 = Resistor [tolerance=±5% resistance=1k package=THT]
  DFRobot_DFPlayer_Mini1 = DFRobot DFPlayer Mini [part_number=DFR0299]
  SP1 = SPEAKER [package=pcb_mount_speaker]
  Q1 = NPN-Transistor [package="TO92 [THT]"]
  R2 = Resistor [tolerance=±5% resistance=330 package=THT]
  LED1 = LEDs [package=led-1206]
  R3 = Resistor [tolerance=±5% resistance=220 package=THT]
  S1 = SPST Switch [package=switch-spdt]
  LED2 = Super Flux LED blue [color=White]
  LED3 = Super Flux LED blue [color=White]
  LED4 = Super Flux LED blue [color=White]
  HLK-PM1 = HLK-PM12 [part_number=HLK-PM12]
  SG1 = Buzzer 12mm [package=buzzer-12mm]
  U1 = MLX90614 [package=to-39]
  hc-sr1 = hc-sr04
  S2 = Toggle Switch [package=THT]
  S3 = Toggle Switch [package=THT]

nets:
  GND: Componente1.GND, DFRobot_DFPlayer_Mini1.GND-1, DFRobot_DFPlayer_Mini1.GND-2, Q1.E, S1.O, LED2.cathode, LED3.cathode, LED4.cathode, HLK-PM1.-Vo, SG1.1, U1.VSS, hc-sr1.GND
  N1: Componente1.D2, R3.Pin_1, S1.P
  N2: Componente1.D3, U1.SCL_VZ
  N3: Componente1.D4, hc-sr1.Trig
  N4: Componente1.D5, S2.L2
  N5: Componente1.D6, hc-sr1.Echo
  N6: Componente1.D7, DFRobot_DFPlayer_Mini1.TX
  N7: Componente1.D8, R1.Pin_0
  N8: Componente1.VIN, LED1.A, HLK-PM1.+Vo, S2.COM, S3.L1
  VCC: Componente1.5V, DFRobot_DFPlayer_Mini1.VCC, R3.Pin_0, U1.VDD, hc-sr1.VCC
  N9: Componente1.A5, S3.L2
  N10: Componente1.A4, R2.Pin_0
  N11: Componente1.A3, DFRobot_DFPlayer_Mini1.BUSY
  N12: R1.Pin_1, DFRobot_DFPlayer_Mini1.RX
  N13: DFRobot_DFPlayer_Mini1.SPK_1, SP1.+
  N14: DFRobot_DFPlayer_Mini1.SPK_2, SP1.-
  N15: Q1.B, R2.Pin_1
  N16: Q1.C, LED1.C
  N17: LED2.anode, LED3.anode, LED4.anode, S2.L1
  N18: SG1.2, S3.COM

notes:
  sirena
  flash intermit
  reles
  PIR
  HC-SR04
  DFPlayer
  flash cegador
  antisabotaje switch

// code stored in the sketch: alarma_guille_PIR_ultrason_2.0.ino
#include "Arduino.h"
#include "SoftwareSerial.h"
#include "DFRobotDFPlayerMini.h"
#include <NewPing.h>


#define busyPin A3 
#define LEDPin 13   
#define TRIGGER_PIN 4 // pin trigger del ultrasonic sensor.    
#define ECHO_PIN 6    // pin echo del ultrasonic sensor.
#define MAX_DISTANCE 75 // distancia maxima de deteccion en cm del ultrasonic sensor
#define intermitentePin 5// pin del flash intermitente
#define PIRPin 3  //pin del sensor PIR
#define flashPin A4// pin de salida para el flash cegador
#define sirenPin A5// pin de salida de la sirena acustica

                                      //pines sensores antisabotaje: 
#define clickAPin 2//el pin 2 conectado con resistencia 330ohm a vcc.
                          //despues puentear con un cable el mismo pin a gnd,
                         //cuando se corta el cable (puente) se activa HIGH
//#define clickBPin 7//        "
//#define clickCPin 8//        "

           //        dfplayer reproductor mp3
           //conectar el rx al pin 8 con resistencia 1k , 
           //y el tx al pin 7  
           
 NewPing sonar(TRIGGER_PIN, ECHO_PIN, MAX_DISTANCE); // NewPin setup de pines del ultrasonic sensor y distancia maxima de deteccion

int mp3 = 0;
int i = 0;
int pirvalue;
int c = 0;
int sabotaje = LOW;  
DFRobotDFPlayerMini myDFPlayer;

void irpir(){ // funcion que lee el PIR y el ultrasonic sensor. si alguno esta activo devuelve high
 
         pirvalue= digitalRead(PIRPin); // lee el PIR
         unsigned int uS = sonar.ping(); // Send ping, get ping time in microseconds (uS).lee ultrasonic sensor
         if (uS / US_ROUNDTRIP_CM != 0 || pirvalue == HIGH) // si alguno de los dos sensores detecta...
         {
           pirvalue = HIGH; // pone activa la señal
           delay(2);
         }
 }
 
void intermitente() { // funcion que dispara la luz intermitente y la sirena acustica
  for (c=0; c<200; c++){ // "c" es el tiempo que dura la sirena y la luz
    irpir();   
    if ((pirvalue == HIGH)||(sabotaje == HIGH)){
     int busyvalue = digitalRead(busyPin); //comprueba si esta sonando el mp3
     if (busyvalue == HIGH){
      c = 0;
    myDFPlayer.play(5); //play ultima pista
     }
  }
    digitalWrite(sirenPin, HIGH);// activa la sirena acustica
    digitalWrite(intermitentePin, HIGH);//doble flash
    delay(60);
    digitalWrite(intermitentePin, LOW);
    delay(75);
    digitalWrite(intermitentePin, HIGH);
    delay(40);
    digitalWrite(intermitentePin, LOW);
    delay(400);
    
  }
  digitalWrite(sirenPin, LOW);// apaga sirena
}
void playalarma() {  //funcion play mp3. cuando es llamada reproduce la pista almacenada en la variable "mp3".
  myDFPlayer.play(mp3);
  delay(100);
}

void deteccion() { //funcion deteccion. bucle de deteccion que activa los protocolos 
  for (long i=0; i<1000; i++) { //espera xxx tiempo para hacer el ciclo de protocolos. mas abajo el delay se multiplica por i
   click_antisabotaje ();// lee sensor antisabotaje
   irpir ();
 
  if ((pirvalue == HIGH)||(sabotaje == HIGH))  //si hay deteccion
  {
    int busyvalue = digitalRead(busyPin);// comprueba que no suene ninguna pista
    if (busyvalue == HIGH){ 
    mp3 = mp3 + 1;//numero de pista mp3
    }
    
    if (i >= 500)//si hay deteccion al final del tiempo de alarma 
    {  
      i=0;          //volvemos a reiniciar el tiempo de alarma
    }  
    if ((mp3 >= 4)||(sabotaje == HIGH))
    {
    myDFPlayer.volume(3); // volumen pista 4
    mp3 = 4;
    sabotaje = LOW;//apaga señal sabotaje
    }

    //int busyvalue= digitalRead(busyPin);
    if (busyvalue == HIGH){
    playalarma();//llama a la funcion play y reproduce la pista de la variable mp3
    delay (1300);//delay para el flash
    digitalWrite(flashPin, HIGH);//doble flash
    delay(40);
    digitalWrite(flashPin, LOW);
    delay(100);
    digitalWrite(flashPin, HIGH);
    delay(60);
    digitalWrite(flashPin, LOW);
       if ((mp3 >= 4)||(sabotaje == HIGH))
   {
     intermitente(); 
   } 
  }  
 }
    delay (70);// retardo que se multiplica por "i" (mas arriba)
  }
} 
void click_antisabotaje() {// funcion antisabotaje. se activa si se corta algun cable de los pines antisabotaje.
 int val1= digitalRead(clickAPin);
// int val2= digitalRead(clickBPin);
// int val3= digitalRead(clickCPin);
 delay(10);
   //if ((val1 || val2 || val3) == HIGH ){
    if (val1 == HIGH ){
   sabotaje = HIGH;// activa señal sabotaje 
  }
} 
void setup(){
    SoftwareSerial mySoftwareSerial(7, 8); // RX, TX
    mySoftwareSerial.begin(9600);
   (!myDFPlayer.begin(mySoftwareSerial));
    myDFPlayer.setTimeOut(350);
    myDFPlayer.outputDevice(DFPLAYER_DEVICE_SD);
  
  delay(1000); // tiempo de inicializacion de la alarma .espera 60segundos para inicializar sensores PIR y ultrasonic
               //y evitar falsos disparos al inicio
  pinMode(PIRPin, INPUT);
  pinMode(busyPin, INPUT);
  pinMode(clickAPin, INPUT);
 // pinMode(clickBPin, INPUT);
  //pinMode(clickCPin, INPUT);
  pinMode(LEDPin, OUTPUT);
  pinMode(sirenPin, OUTPUT);
  pinMode(flashPin, OUTPUT); 
  pinMode(intermitentePin, OUTPUT);
  
}
 
void loop(){
   mp3 = 0;
   myDFPlayer.volume(2);
   digitalWrite(sirenPin, LOW);// apaga sirena
   click_antisabotaje ();// lee sensor antisabotaje
   irpir(); // lee sensores PIR y ultrasonic

  if ((pirvalue == HIGH)||(sabotaje == HIGH))
  {
    deteccion();
  }
}
